# Fritzing sketch project (saved by Fritzing 1.0.0d)
breadboards: 2

parts:
  U1 = ESP32-38PinWide [part_number=ESP32-38PinWide]
  S1 = Humiture Sensor v1.0 [package=THT]
  A1 = Waveshare 1.54in epaper display  # not connected
  A2 = Waveshare e-Paper HAT [package=THT]  # not connected
  YL-83_-_Control_Board1 = YL-83 Rain Sensor - Control Board
  YL-83_-_Detection_Board1 = YL-83 Rain Sensor - Detection Board
  Part1 = Barometric Pressure Sensor - BMP180 Breakout (GY-68)
  Part2 = Adafruit SGP30 [part_number="Adafruit #3709"]
  Capacitive_Soil_Moisture_Sensor1 = DFRobot Capacitive Soil Moisture Sensor V1.0 [part_number=SEN0193]
  U2 = LIPO-110mAh [package=lipo-110]  # not connected

nets:
  VCC: U1.3.3, S1.S, YL-83_-_Control_Board1.VCC, Part1.SCL, Part2.VCC
  N1: U1.GPIO36, YL-83_-_Control_Board1.AO
  N2: U1.GPIO34, Capacitive_Soil_Moisture_Sensor1.A
  N3: U1.GPIO32, S1.+
  N4: U1.GPIO25, YL-83_-_Control_Board1.DO
  GND: U1.GND, S1.-, YL-83_-_Control_Board1.GND, Part1.SDA, Part2.GND
  N5: U1.GPIO21, Part1.VCC, Part2.SCL
  N6: U1.GPIO22, Part1.GND, Part2.SDA
  N7: YL-83_-_Control_Board1.POS, YL-83_-_Detection_Board1.POS
  N8: YL-83_-_Control_Board1.NEG, YL-83_-_Detection_Board1.NEG

notes:
  22 = SCL
  21 = SDA
  Raindrop sensor got removed in V1.0

custom parts:
  ESP32-38PinWide: Generic 38-Pin ESP32 with wide format (only access to one side of pins on a breadboard) based on Stephen Lilley's HiLetgo ESP-WROOM-32 ESP32 ESP-32S Development Board.
  Humiture Sensor v1.0: Humiture Sensor www.sunfounder.com
  Waveshare 1.54in epaper display: This is an E-Ink display module, 1.54inch, 200x200 resolution, with embedded controller, communicating via SPI interface.
  Waveshare e-Paper HAT: .This is a universal driver board for e-Paper raw panels, can be used to drive various SPI interface e-Paper from Waveshare.
  YL-83 Rain Sensor - Control Board: The YL-83 is a rain sensor that has more resistance when dry and less resistance when wet. The module runs at 5V.
  YL-83 Rain Sensor - Detection Board: The YL-83 is a rain sensor that has more resistance when dry and less resistance when wet. The module runs at 5V.
  Adafruit SGP30: Breathe easy with the SGP30 Multi-Pixel Gas Sensor, a fully integrated MOX gas sensor. This is a very fine air quality sensor from the sensor experts at Sensirion, with I2C interfacing and fully calibrated output signals with a typical accuracy of 15% within measured values. The SGP combines multiple metal-oxide sensing elements on one chip to provide more detailed air quality signals. This is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
  DFRobot Capacitive Soil Moisture Sensor V1.0: DFRobot Capacitive Soil Moisture Sensor V1.0 This product measures soil moisture levels by capacitive sensing, rather than resistive sensing like other types of moisture sensor. It is made of a corrosion resistant material giving it a long service life. Insert it into soil and impress your friends with the real-time soil moisture data! The product includes an on-board voltage regulator which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
